# Fritzing sketch DHT22-rpi (saved by Fritzing 0.9.3b)
breadboards: 1

parts:
  Raspberry_Pi1 = Raspberry Pi 2
  RHT1 = Humidity and Temperature Sensor RHT03
  R1 = Resistor [tolerance=±5% resistance=10k package=THT]

nets:
  3V3: Raspberry_Pi1.3v3, RHT1.Vcc, R1.Pin_0
  N1: Raspberry_Pi1.GND, RHT1.GND_2
  N2: Raspberry_Pi1.GPIO23, RHT1.Data-signal, R1.Pin_1

notes:
  Temp : 23.3°C, Humidity 33.7%
  10k Ohm
  DH22T
